# Fritzing sketch FootSwitchController (saved by Fritzing 0.9.9b)
breadboards: 1

parts:
  IC1 = seeeduino-xiao
  U1 = mini DIN 6 Connector [package=mini-din6]
  R1 = Resistor [tolerance=±5% power=0.25W resistance=2.2k package=THT]
  R2 = Resistor [tolerance=±5% power=0.25W resistance=2.2k package=THT]
  R3 = Resistor [tolerance=±5% power=0.25W resistance=2.2k package=THT]
  J1 = female pin header, 7 pins [form="♀ (female)"]
  J2 = female pin header, 7 pins [form="♀ (female)"]

nets:
  N1: IC1.D0, J2.pin1
  N2: IC1.D1, U1.5, R1.Pin_1, J2.pin2
  N3: IC1.D2, U1.1, R2.Pin_1, J2.pin3
  N4: IC1.D3, U1.2, R3.Pin_1, J2.pin4
  N5: IC1.D4, J2.pin5
  N6: IC1.D5, J2.pin6
  N7: IC1.D6, J2.pin7
  N8: IC1.D7, J1.pin7
  N9: IC1.D8, J1.pin6
  N10: IC1.D9, J1.pin5
  N11: IC1.D10, J1.pin4
  N12: IC1.3V3, R1.Pin_0, R2.Pin_0, R3.Pin_0, J1.pin3
  N13: IC1.GND, U1.3, U1.6, J1.pin2
  N14: IC1.5V, J1.pin1

custom parts:
  seeeduino-xiao: Seeeduino XIAO processor board.

// code stored in the sketch: ClickSetButton_With_FootSwitch.ino
/*
  Copyright (c) 2014-2015 NicoHood
  See the readme for credit to other people.

  Mouse example
  Press a button to click or move the mouse.

  You may also use BootMouse to enable a bios compatible (single report) mouse.
  However this is very unusual and not recommended.
  Bios mice dont support wheels which can cause problems after a reboot.

  See HID Project documentation for more Information.
  https://github.com/NicoHood/HID/wiki/Mouse-API
*/

#include "HID-Project.h"
#include <TimerTC3.h>

#define SERIAL_BAUDRATE (115200)
#define TC3_INT_COUNT   (10 * 1000)  // microsecond
#define AD_RESOLUTION   (10)
#define HORIZ_POS_ADJ   (1920)
#define VERT_POS_ADJ    (1760)
#define BTN_POS_DIFF    (720)
#define MOUSE_MOVE_ITR  (5)
#define DAMPER_PEDAL_UNPUSHED     (642)
#define DAMPER_PEDAL_PUSHED       (374)
#define SOSTENUTO_PEDAL_UNPUSHED  (1023)
#define SOSTENUTO_PEDAL_PUSHED    (180)
#define SOFT_PEDAL_UNPUSHED       (1023)
#define SOFT_PEDAL_PUSHED         (160)
#define PIN_IN_DAMPER_PEDAL     (1)
#define PIN_IN_SOSTENUTO_PEDAL  (2)
#define PIN_IN_SOFT_PEDAL       (3)
#define NUM_OF_EDGE             (1)
#define NUM_OF_DEBOUNCE         (3)
#define NUM_OF_POLLING          (NUM_OF_EDGE + NUM_OF_DEBOUNCE)

// buttons name on Yukarinette Connector Voice Recognition Window
typedef enum TAG_BUTTON_NAME
{
  LANG_1ST,   // 1st language: Japanese (default)
  LANG_2ND,   // 2nd language: English US (default)
  LANG_3RD,   // 3rd language: Chinese Mainland (default)
  LANG_MAX
}button_number_t;

typedef enum TAG_PEDAL_NUMBER
{
  PEDAL_DAMPER,     // right pedal
  PEDAL_SOSTENUTO,  // middle pedal
  PEDAL_SOFT,       // left pedal
  PEDAL_MAX
}pedal_number_t;

typedef enum TAG_PEDAL_COND
{
  PEDAL_COND_DONT_CARE,     // unpushed or continuing pushed
  PEDAL_COND_PUSHED_EDGE,   // detect pushed edge
  PEDAL_COND_PUSHED,        // pushed
  PEDAL_COND_MAX
}pedal_cond_t;

typedef struct TAG_ANALOG_PEDAL
{
  uint32_t ulPinIndicator;        // indicator led output: ON when pedal pushed
  uint32_t ulPinPedal;            // pedal analog input
  uint16_t usThresholdPushed;     // pedal threshold when pedal pushed
  uint16_t usThresholdUnpushed;   // pedal threshold when pedal unpushed
  bool bIsPushedPoll[NUM_OF_POLLING];  // debounce polling pattern: true when pedal pushed
  pedal_cond_t kPedalCond;        // pedal condition
  uint8_t ucPushedCount;          // number of pushed
  uint8_t ucPollCount;            // polling counter: 0 to NUM_OF_POLLING -1
}analog_pedal_t;

analog_pedal_t kPedal[PEDAL_MAX] = 
{
  { // damper pedal (right pedal) setting
    PIN_LED,
    PIN_IN_DAMPER_PEDAL,
    DAMPER_PEDAL_PUSHED,
    DAMPER_PEDAL_UNPUSHED,
    {false, false, false, true},  // 4th element prevents from PUSHED detection when started with pedal pushing
    PEDAL_COND_DONT_CARE,
    0,
    0
  },
  { // sostenuto pedal (middle pedal) setting
    PIN_LED2,
    PIN_IN_SOSTENUTO_PEDAL,
    SOSTENUTO_PEDAL_PUSHED,
    SOSTENUTO_PEDAL_UNPUSHED,
    {false, false, false, true},  // 4th element prevents from PUSHED detection when started with pedal pushing
    PEDAL_COND_DONT_CARE,
    0,
    0
  },
  { // soft pedal (left pedal) setting
    PIN_LED3,
    PIN_IN_SOFT_PEDAL,
    SOFT_PEDAL_PUSHED,
    SOFT_PEDAL_UNPUSHED,
    {false, false, false, true},  // 4th element prevents from PUSHED detection when started with pedal pushing
    PEDAL_COND_DONT_CARE,
    0,
    0
  }
};

void MouseMoveAndClick(button_number_t);
void vPedalDiscriminant(pedal_number_t, button_number_t);
void vInputPoll(void);

void setup()
{
  SerialUSB.begin(SERIAL_BAUDRATE, SERIAL_8N1); // default SERIAL_8N1
  while(!SerialUSB)
  {
    ; // wait for SerialUSB enabled
  }
  SerialUSB.print("serial com opened as ");
  SerialUSB.print("baudrate: ");
  SerialUSB.print(SERIAL_BAUDRATE);
  SerialUSB.println(", data bit: 8, parity bit: none, stop bit: 1");

  pinMode(kPedal[PEDAL_DAMPER].ulPinIndicator, OUTPUT);
  SerialUSB.print("set damper pedal indicator OUTPUT #");
  SerialUSB.println(kPedal[PEDAL_DAMPER].ulPinIndicator);
  pinMode(kPedal[PEDAL_SOSTENUTO].ulPinIndicator, OUTPUT);
  SerialUSB.print("set sostenuto pedal indicator OUTPUT #");
  SerialUSB.println(kPedal[PEDAL_SOSTENUTO].ulPinIndicator);
  pinMode(kPedal[PEDAL_SOFT].ulPinIndicator, OUTPUT);
  SerialUSB.print("set soft pedal indicator OUTPUT #");
  SerialUSB.println(kPedal[PEDAL_SOFT].ulPinIndicator);

  pinMode(kPedal[PEDAL_DAMPER].ulPinPedal, INPUT);
  SerialUSB.print("set damper pedal analog INPUT #");
  SerialUSB.println(kPedal[PEDAL_DAMPER].ulPinPedal);
  pinMode(kPedal[PEDAL_SOSTENUTO].ulPinPedal, INPUT);
  SerialUSB.print("sostenuto pedal analog INPUT #");
  SerialUSB.println(kPedal[PEDAL_SOSTENUTO].ulPinPedal);
  pinMode(kPedal[PEDAL_SOFT].ulPinPedal, INPUT);
  SerialUSB.print("soft pedal analog INPUT #");
  SerialUSB.println(kPedal[PEDAL_SOFT].ulPinPedal);

  analogReadResolution(AD_RESOLUTION);  // default 10-bit on Seeeduino XIAO
  SerialUSB.print("set A/D converter resolution: ");
  SerialUSB.print(AD_RESOLUTION);
  SerialUSB.println(" bits");

  AbsoluteMouse.begin();
  SerialUSB.println("absolute positioning mouse started");
  
  Mouse.begin();
  SerialUSB.println("relative positioning mouse started");

  TimerTc3.initialize(TC3_INT_COUNT);
  TimerTc3.attachInterrupt(vInputPoll);
}

void loop()
{
  ;
}

void MouseMoveAndClick(button_number_t kButtonNumber)
{
  AbsoluteMouse.moveTo(SHRT_MAX - HORIZ_POS_ADJ,
                        VERT_POS_ADJ + kButtonNumber * BTN_POS_DIFF);
  for(int i = 0; i < MOUSE_MOVE_ITR; i++)
  {
    Mouse.move(SCHAR_MAX, 0);
  }
  Mouse.click();

  return;
}

void vPedalDiscriminant(pedal_number_t pedal_idx, button_number_t button_idx)
{
  uint8_t ucPollCountPrev = (kPedal[pedal_idx].ucPollCount + NUM_OF_POLLING - 1) % NUM_OF_POLLING;
  uint32_t ulPedalVal = analogRead(kPedal[pedal_idx].ulPinPedal);

  kPedal[pedal_idx].bIsPushedPoll[kPedal[pedal_idx].ucPollCount]
    = (ulPedalVal < kPedal[pedal_idx].usThresholdPushed) ? true : false;

  switch (kPedal[pedal_idx].kPedalCond)
  {
    case PEDAL_COND_DONT_CARE:
      if ((!kPedal[pedal_idx].bIsPushedPoll[ucPollCountPrev])
        && (kPedal[pedal_idx].bIsPushedPoll[kPedal[pedal_idx].ucPollCount]))
      {
        kPedal[pedal_idx].kPedalCond = PEDAL_COND_PUSHED_EDGE;
        kPedal[pedal_idx].ucPushedCount = 1;
      }
      break;
    case PEDAL_COND_PUSHED_EDGE:
      if (kPedal[pedal_idx].bIsPushedPoll[kPedal[pedal_idx].ucPollCount])
      {
        if (NUM_OF_DEBOUNCE == ++kPedal[pedal_idx].ucPushedCount)
        {
          kPedal[pedal_idx].kPedalCond = PEDAL_COND_PUSHED;
        }
      }
      else
      {
        kPedal[pedal_idx].kPedalCond = PEDAL_COND_DONT_CARE;
      }
      break;
    case PEDAL_COND_PUSHED:
      MouseMoveAndClick(button_idx);
    default:
      kPedal[pedal_idx].kPedalCond = PEDAL_COND_DONT_CARE;
      kPedal[pedal_idx].ucPushedCount = 0;
      break;
  }

  kPedal[pedal_idx].ucPollCount = (kPedal[pedal_idx].ucPollCount + 1) % NUM_OF_POLLING;

  return;
}

void vInputPoll(void)
{
  vPedalDiscriminant(PEDAL_DAMPER, LANG_1ST);
  vPedalDiscriminant(PEDAL_SOSTENUTO, LANG_2ND);
  vPedalDiscriminant(PEDAL_SOFT, LANG_3RD);

  return;
}
